// Digital circuit main.dig as structural Verilog
module main (
  input  clk
);

  wire AI, alu_1_p2, AO, BI, BO, carry, DATA, EO, RAO, RBO, reg_a_1_p5, SU, zero;
  wire [7:0] ROM_A_d, ROM_B_d;
  wire [10:0] undriven;

  EEPROM #(.AddrBits(11), .Bits(8)) ROM_A (.A(undriven), .D(ROM_A_d));  // open: CS, WE, OE
  EEPROM #(.AddrBits(11), .Bits(8)) ROM_B (.A(undriven), .D(ROM_B_d));  // open: CS, WE, OE
  assign DATA = RAO ? ROM_A_d[0] : 1'bz;  // Driver driver_1
  assign DATA = RBO ? ROM_B_d[0] : 1'bz;  // Driver driver_2
  // REG_A reg_a_1: pin names not known; wires that end beside it: DATA, clk, AI, AO, reg_a_1_p5, DATA
  // ALU alu_1: pin names not known; wires that end beside it: reg_a_1_p5, alu_1_p2, SU, EO, DATA, carry, zero
  // REG_B reg_b_1: pin names not known; wires that end beside it: DATA, clk, BI, BO, alu_1_p2, DATA
  // Pins of 1 and 8 bits meet at ROM_A_d
  // Pins of 1 and 8 bits meet at ROM_B_d

  // Notes on the sheet:
  //   clk: Hz: 5
endmodule
